# Fritzing sketch logger schema (saved by Fritzing 0.9.3b)
breadboards: 2

parts:
  Grove1 = Grove OLED 128x96
  sdCard1 = my_sdCard
  S3 = Pushbutton [package="[SMD]"]
  S4 = Pushbutton [package="[SMD]"]
  S5 = Pushbutton [package="[SMD]"]
  U1 = NodeMCU V3.0
  Componente1 = ADS1115
  IC1 = DS1307 [package=THT]
  XTAL1 = CRYSTAL - kHz [frequency="32 kHz"]
  BAT1 = Battery Holders [package=battcom_20mm_pth]
  R1 = Resistor [tolerance=±5% resistance=220 package="0805 [SMD]"]
  R2 = Resistor [tolerance=±5% resistance=220 package="0805 [SMD]"]
  J1 = Piezo Speaker
  U2 = LIPO-2000mAh [package=lipo-2000]
  Mod1 = TP4056 [part_number=TP4056]

nets:
  GND: Grove1.GND, sdCard1.GND, S3.Pin_3, S3.Pin_4, S4.Pin_3, S4.Pin_4, S5.Pin_3, S5.Pin_4, U1.GND, Componente1.GND, IC1.0V, BAT1.-, J1.pin1, Mod1.pin6
  VCC: Grove1.VCC, sdCard1.VCC, Componente1.VDD, IC1.X1_-_Crystal, Mod1.pin3
  N1: Grove1.SDA, U1.D1, Componente1.SDA, IC1.SCL_-_I2C_Clock
  N2: Grove1.SCL, U1.D2, Componente1.SCL, IC1.SWQ/OUT_-_Clock_Output
  N3: sdCard1.MISO, U1.S1
  N4: sdCard1.MOSI, U1.S0
  N5: sdCard1.SCK, U1.SK
  N6: sdCard1.CS, U1.SC
  N7: S3.Pin_1, S3.Pin_2, U1.D8
  N8: S4.Pin_1, S4.Pin_2, U1.D7
  N9: S5.Pin_1, S5.Pin_2, U1.D6
  N10: Componente1.A0, R1.Pin_0, R2.Pin_0
  N11: IC1.X2_-_Crystal, XTAL1.pin_1
  N12: IC1.Vbat_-_Backup_Supply, XTAL1.pin_0
  N13: IC1.SDA_-_I2C_Data, BAT1.+
  N14: U2.+, Mod1.pin4
  N15: U2.-, Mod1.pin5

custom parts:
  my_sdCard: micro sdCard Adapter with 90º pin header. Use a filtering Capacitor between CS and GND if needed. PCB View Pinouts are Reversed for laying parallel on PCB using a 90º pin header.
  NodeMCU V3.0: ESP8266 based NodeMCU
  ADS1115: ADC ADS1115
  TP4056: TP4056 Lithium battery charger / protection module. (this one has the pins on .1 boundaried unlike the original)
